// Logisim project spear1.circ as structural Verilog: 1 circuit, main circuit main
module main (
);

  wire and_1_out, and_2_out, and_3_out, and_4_out, and_5_out, and_6_out, and_12_out, and_13_out, and_14_out,
       and_15_out, button_1_out, button_2_out, button_3_out, button_4_out, button_5_out, CLK, clock_1_out,
       d_ff_1_q, d_ff_1_qn, IR_OE, not_1_out, not_2_out, not_4_out, not_5_out, not_6_out, not_7_out,
       not_8_out, or_2_out, or_3_out, or_4_out, or_5_out, or_6_out, or_7_out, R1, R2, R3, R4, R7;
  wire [7:0] A, adder_2_out, adder_3_out, B, BUS, CW, not_3_out, RAM_P, rom_2_data;
  wire [15:0] adder_1_out, controlled_buffer_1_out, IR;
  wire [15:8] IR_O;

  Button button_1 (.out(button_1_out));
  Clock clock_1 (.out(clock_1_out));
  Button button_2 (.out(button_2_out));
  and and_1 (and_1_out, clock_1_out, d_ff_1_q);
  D_Flip_Flop d_ff_1 (
    .clk(button_2_out), .D(d_ff_1_qn), .Q(d_ff_1_q), .Qn(d_ff_1_qn), .en(1'b1));  // open: preset, reset
  Register #(.width(16)) register_1 (.D(controlled_buffer_1_out), .en(1'b1), .Q(IR), .clk(CLK), .clr(button_3_out));
  Button button_3 (.out(button_3_out));
  or or_1 (CLK, button_1_out, and_1_out);
  not not_1 (not_1_out, IR_OE);
  assign controlled_buffer_1_out = not_1_out ? adder_1_out : 16'bz;  // Controlled_Buffer controlled_buffer_1
  Adder #(.width(16)) adder_1 (.a(IR), .b(16'h1), .out(adder_1_out));  // open: cin, cout
  Pull_Resistor pull_resistor_1 (.node(controlled_buffer_1_out));
  ROM #(.addrWidth(16)) rom_1 (.addr(IR), .data(CW));  // open: sel
  ROM #(.addrWidth(16)) rom_2 (.addr(IR), .data(rom_2_data));  // open: sel
  or or_2 (or_2_out, CW[4], CW[5], CW[6], CW[7]);
  assign controlled_buffer_1_out = IR_OE ? {IR_O, BUS} : 16'bz;  // Controlled_Buffer controlled_buffer_2
  assign BUS = not_2_out ? rom_2_data : 8'bz;  // Controlled_Buffer controlled_buffer_3
  not not_2 (not_2_out, or_2_out);
  Adder adder_2 (.a(A), .b(B), .out(adder_2_out));  // open: cin, cout
  assign not_3_out = ~A;  // NOT_Gate not_3, 8 bits wide
  assign BUS = CW[5] ? RAM_P : 8'bz;  // Controlled_Buffer controlled_buffer_4
  Register register_2 (.D(BUS), .en(CW[1]), .Q(RAM_P), .clk(CLK));  // open: clr
  Register register_3 (.D(BUS), .en(CW[2]), .Q(A), .clk(CLK));  // open: clr
  Register register_4 (.D(BUS), .en(CW[3]), .Q(B), .clk(CLK));  // open: clr
  assign BUS = CW[6] ? adder_2_out : 8'bz;  // Controlled_Buffer controlled_buffer_5
  Adder adder_3 (.a(not_3_out), .b(8'h1), .out(adder_3_out));  // open: cin, cout
  assign BUS = CW[7] ? adder_3_out : 8'bz;  // Controlled_Buffer controlled_buffer_6
  or or_3 (or_3_out, R1, R2, R3, R4, R7);
  or or_4 (or_4_out, RAM_P[3], RAM_P[4], RAM_P[5], RAM_P[6], RAM_P[7]);
  not not_4 (not_4_out, or_3_out);
  or or_5 (or_5_out, CW[0], CW[4]);
  not not_5 (not_5_out, or_4_out);
  and and_2 (and_2_out, RAM_P[0], not_5_out);
  and and_3 (and_3_out, RAM_P[1], not_5_out);
  and and_4 (and_4_out, RAM_P[2], not_5_out);
  and and_5 (and_5_out, not_4_out, or_5_out);
  and and_6 (and_6_out, CLK, CW[0]);
  not not_6 (not_6_out, and_2_out);
  not not_7 (not_7_out, and_3_out);
  not not_8 (not_8_out, and_4_out);
  RAM ram_1 (.addr(RAM_P), .data(BUS), .sel(and_5_out), .clk(and_6_out), .ld(CW[4]), .clr(button_4_out));
  Button button_4 (.out(button_4_out));
  and and_7 (R1, and_2_out, not_7_out, not_8_out);
  and and_8 (R2, not_6_out, and_3_out, not_8_out);
  and and_9 (R3, and_2_out, and_3_out, not_8_out);
  and and_10 (R4, not_6_out, not_7_out, and_4_out);
  and and_11 (R7, and_2_out, and_3_out, and_4_out);
  TTY tty_1 (.data(BUS[6:0]), .clk(CLK), .we(and_12_out), .clr(button_5_out));
  and and_12 (and_12_out, R7, CW[0]);
  and and_13 (and_13_out, R3, A[7]);
  and and_14 (and_14_out, R4, A[7]);
  Button button_5 (.out(button_5_out));
  or or_6 (or_6_out, R1, and_13_out);
  and and_15 (and_15_out, or_6_out, CW[0]);
  or or_7 (or_7_out, R2, and_14_out);
  and and_16 (IR_OE, or_7_out, CW[0]);
  Register register_5 (.D(BUS), .en(and_15_out), .Q(IR_O), .clk(CLK));  // open: clr

  // Other names for the same wires on the sheet: IR_O[7:0] = BUS

  // Notes on the sheet:
  //   contents of rom_1 (hex, n*v repeats v):
  //   2 1 2 1 0 2 14 8 2 41 2 1 2 18 2 14 84 44 8 2 1 2 1 84 2 1 2 1 2 1 2 1 2 1 0 2 1 0 2 14 8 44 2 1 2 1
  //   2 1 2 1 2 1 0 2 14 8 2 41 2 14 8 2 41 2 1 2 18 2 14 84 44 8 2 1 2 1 2 1 2 1 2 1 0 2 1 0 2 14 8 44 2
  //   1 2 1 2 1 2 1 2 14 8 2 41 2 18 2 14 84 2 41 0 2 1 2 14 8 2 41 0 2 14 8 2 41 2 1 2 18 2 14 84 44 8 84
  //   2 1 2 1 2 1 2 1 2 1 0 2 1 0 2 14 8 44 2 1 2 1 2 14 8 2 41 2 1 2 18 2 14 2 41 2 14 8 2 41 2 1 2 14 8
  //   2 41 2 1 0 2 14 2 1 2 1 2 14 8 41 2 14 84 2 18 41 2 1 2 1 0 2 1 2 1 0 2 14 8 2 41 2 1 2 18 2 14 84 2
  //   41 0 2 14 8 2 41 2 1 2 18 2 14 84 44 8 84 8 44 2 1 2 1 2 1 2 1 2 1 0 2 1 0 2 14 8 44 2 1 2 1 2 14 8
  //   2 41 2 1 0 2 14 8 2 41 2 14 8 2 41 2 18 2 14 84 44 8 2 1 2 1 2 1 2 1 2 1 0 2 1 0 2 14 8 44 2 1 2 1 2
  //   14 8 2 41 2 1 2 14 8 2 41 2 1 0 2 14 2 1 2 1 2 14 8 41 2 14 84 2 18 41 2 1 2 1 0 2 14 8 2 41 2 1 2
  //   18 2 14 2 41 2 1 2 1 0 2 1 2 14 8 2 41 2 1 0 2 14 2 1 2 1 2 14 84 2 18 41 2 1 2 1 0 2 14 2 18 41 2
  //   18 2 14 2 41 2 14 8 2 41 2 1 2 18 2 14 84 2 41 2 1 2 1 0 0 2 14 8 2 41 2 14 2 41 0 2 1 0 2 1 2 14 8
  //   44 2 1 2 1 2 1 0 2 14 8 2 41 2 1 2 18 2 14 84 44 8 8 44 2 1 2 1 2 1 2 1 2 1 0 2 1 0 2 14 8 44 2 1 2
  //   1 2 1 0 2 14 8 2 41 2 14 8 2 41 2 18 2 14 84 44 8 2 1 2 1 2 1 2 1 2 1 0 2 1 0 2 14 8 44 2 1 2 1 2 14
  //   8 2 41 2 14 8 2 41 0 2 14 2 1 2 1 2 14 84 2 18 41 2 1 2 1 0 2 14 2 18 41 2 1 2 18 2 14 84 44 8 2 1 2
  //   1 84 2 1 2 1 2 1 2 1 2 1 0 2 1 0 2 14 8 44 2 1 2 1 2 1 2 1 0 2 14 8 2 41 2 1 2 18 2 14 2 41 2 1 2 1
  //   0 2 14 8 2 41 2 1 2 1 2 1 2 1 0 2 1 1 1 2 14 8 2 41 2 1 2 18 2 14 2 41 0 2 14 8 2 41 2 1 2 18 2 14 2
  //   41 2 1 2 1 0 2 1 2 1 0 2 7*1 2 14 8 2 41 2 1 2 1 2 1 2 1 0 0 2 1 2 1
  //   contents of rom_2 (hex, n*v repeats v):
  //   1 1 2 b0 0 e 0 0 8 0 9 0 8 0 9 4*0 3 0 4 22 0 3 0 4 22 8 1 1 0 2 25 0 8 0 0 8 0 ff 0 3 0 4 34 7 30 1
  //   1 2 a6 0 e 0 0 f 0 f 0 0 8 0 9 0 8 0 9 4*0 3 0 4 52 8 0 1 0 2 55 0 8 1 0 8 0 ff 0 3 0 4 6e 7 2d 8 0
  //   e 0 0 9 0 8 0 9 0 0 f 0 0 11 0 f 0 0 10 0 0 10 0 0 8 0 9 0 8 0 9 5*0 3 0 4 90 8 0 1 0 2 93 0 8 1 0 8
  //   0 ff 0 3 0 4 d1 11 0 0 8 0 9 1 8 0 9 0 11 0 10 0 0 8 0 9 a 8 0 0 d 0 10 ff 0 d 0 3 0 4 cc 10 0 1 0 9
  //   0 0 d 0 0 1 0 2 b7 0 1 0 2 76 0 11 0 0 8 0 9 1 8 0 9 0 0 12 0 0 12 0 0 8 0 9 0 8 0 9 5*0 ff 0 3 0 4
  //   fc 8 0 1 0 2 ff 0 8 1 0 8 0 ff 0 3 1 4 a5 f 0 0 14 0 13 0 0 13 0 0 8 0 12 0 0 9 0 8 0 9 4*0 3 1 4 2b
  //   8 0 1 1 2 2e 0 8 1 0 8 0 ff 0 3 1 4 6c 14 0 0 8 0 9 a 8 0 0 d 0 14 ff 0 d 0 3 1 4 5a 14 0 1 0 9 0 0
  //   d 0 0 1 1 2 45 0 13 0 0 8 0 9 1 8 0 9 0 13 0 1 1 2 f 0 8 30 14 0 0 9 0 a a 0 9 0 3 1 4 87 a 0 0 9 0
  //   0 1 1 2 76 0 a 0 9 0 0 8 0 9 0 7 0 12 0 0 8 0 9 1 8 0 9 0 0 12 0 1 0 2 e0 0 0 5 0 0 1 0 6 0 2 0 0 15
  //   0 0 8 1 8 0 ff 0 3 2 4 a3 16 2 0 16 0 0 8 0 9 7f 8 0 9 4*0 ff 0 3 1 4 db 8 0 1 1 2 de 0 8 1 0 8 0 ff
  //   0 3 2 4 9e 17 2 0 17 0 0 8 0 16 0 0 9 0 8 0 9 4*0 3 2 4 5 8 0 1 2 2 8 0 8 1 0 8 0 ff 0 3 2 4 6c 16 0
  //   0 8 0 17 0 0 9 0 0 8 0 3 2 4 2c 9 0 0 8 0 0 1 2 2 1b 0 9 0 8 0 0 9 0 8 0 9 4*0 3 2 4 4a 0 3 2 4 4a 8
  //   1 1 2 2 4d 0 8 0 0 8 0 ff 0 3 2 4 5a 1 2 2 8c 0 17 0 0 8 0 9 1 8 0 9 0 17 0 1 1 2 e9 0 16 0 0 e 0 5
  //   2 6 7a 1 0 2 4 0 7 20 2f 20 15 0 0 8 0 9 1 8 0 9 0 15 0 0 16 0 0 8 0 9 1 8 0 9 0 16 0 1 1 2 c0 0 1 1
  //   2 b3 0 7 74 6f 74 61 6c 3a 20 15 0 0 e 0 5 2 6 b9 1 0 2 4 0 0 1 2 2 ba
endmodule
