// Logisim project spear74.circ as structural Verilog: 1 circuit, main circuit main
module main (
);

  wire A0, A1, A2, A3, A4, A5, A6, A7, A_INV0, A_INV1, A_INV2, A_INV3, A_INV4, A_INV5, A_INV6, A_INV7,
       A_NEG0, A_NEG1, A_NEG2, A_NEG3, A_NEG4, A_NEG5, A_NEG6, A_NEG7, AC0, AC1, AC2, AC3, AC4, AC5, AC6,
       AC7, ADD0, ADD1, ADD2, ADD3, ADD4, ADD5, ADD6, ADD7, ADDC7, B0, B1, B2, B3, B4, B5, B6, B7, BUS0,
       BUS1, BUS2, BUS3, BUS4, BUS5, BUS6, BUS7, C_RP0, C_RP0_INV, C_RP1, C_RP1_INV, C_RP2, C_RP2_INV, CLK,
       CLK2, CLK_HW, CW0, CW1, CW2, CW3, CW4, CW4_INV, CW5, CW6, CW7, dip_74283_1_p17, ic_7408_8_p6,
       ic_7408_8_p7, ic_7408_9_p4, ic_7408_9_p5, ic_7408_9_p10, ic_7408_9_p11, IR0, IR1, IR2, IR3, IR4, IR5,
       IR6, IR7, IR8, IR9, IR10, IR11, IR12, IR13, IR14, IR15, IR_IN0, IR_IN1, IR_IN2, IR_IN3, IR_IN4,
       IR_IN5, IR_IN6, IR_IN7, IR_IN8, IR_IN9, IR_IN10, IR_IN11, IR_IN12, IR_IN13, IR_IN14, IR_IN15, IR_O8,
       IR_O9, IR_O10, IR_O11, IR_O12, IR_O13, IR_O14, IR_O15, IR_OE, IR_OE_INV, IRC0, IRC1, IRC2, IRC3, IRC4,
       IRC5, IRC6, IRC7, IRC8, IRC9, IRC10, IRC11, IRC12, IRC13, IRC14, IRC15, IRI0, IRI1, IRI2, IRI3, IRI4,
       IRI5, IRI6, IRI7, IRI8, IRI9, IRI10, IRI11, IRI12, IRI13, IRI14, IRI15, LIT0, LIT1, LIT2, LIT3, LIT4,
       LIT5, LIT6, LIT7, LIT_EN, nor_3_out, not_8_out, not_9_out, not_10_out, R1, R1_INV, R2, R2_INV, R3, R4,
       R7, RAM_EN, RAM_EN_INV, RAM_WE, RAM_WE_INV, READ_A, READ_B, READ_IR_O, READ_RP, RP0, RP1, RP2, RP3,
       RP4, RP5, RP6, RP7, RST;

  Clock clock_1 (.out(CLK));
  Button button_1 (.out(RST));
  TTY tty_1 (.data({BUS6, BUS5, BUS4, BUS3, BUS2, BUS1, BUS0}), .clk(CLK_HW));  // open: we, clr
  // IC_74374 ic_74374_1: pin names not known; wires that end beside it: IR_IN0, IR_IN1, IR_IN2, IR_IN3, IR_IN4, IR_IN5, IR_IN6, IR0, IR1, IR2, IR3, IR4, IR5, IR6
  // IC_7486 ic_7486_1: pin names not known; wires that end beside it: IR_IN7, CLK2, IR0, IR1, IR2, IR3, 1'b1, 1'b0, IR7, IRI0, IRI1, IRI2, IRI3
  // IC_7486 ic_7486_2: pin names not known; wires that end beside it: IRC0, IRC1, IRC2, IR4, IR5, IR6, IR7, IRC3, IRC4, IRC5, IRC6, IRI4, IRI5, IRI6, IRI7
  // NOT_Gate not_1 has open pins: in=LIT_EN, out=open
  ROM #(.addrWidth(16)) rom_1 (
    .addr({IR15, IR14, IR13, IR12, IR11, IR10, IR9, IR8, IR7, IR6, IR5, IR4, IR3, IR2, IR1, IR0}),
    .data({CW7, CW6, CW5, CW4, CW3, CW2, CW1, CW0}));  // open: sel
  ROM #(.addrWidth(16)) rom_2 (
    .addr({IR15, IR14, IR13, IR12, IR11, IR10, IR9, IR8, IR7, IR6, IR5, IR4, IR3, IR2, IR1, IR0}),
    .data({LIT7, LIT6, LIT5, LIT4, LIT3, LIT2, LIT1, LIT0}));  // open: sel
  // DIP_74373 dip_74373_1: pin names not known; wires that end beside it: BUS0, LIT0, LIT1, BUS1, BUS2, LIT2, LIT3, BUS3, BUS7, LIT7, LIT6, BUS6, BUS5, LIT5, LIT4, BUS4, 1'b1
  // IC_74374 ic_74374_2: pin names not known; wires that end beside it: IR_IN8, IR_IN9, IR_IN10, IR_IN11, IR_IN12, IR_IN13, IR_IN14, IR8, IR9, IR10, IR11, IR12, IR13, IR14
  // IC_7408 ic_7408_1: pin names not known; wires that end beside it: IR_IN15, CLK2, IR0, IR1, IR2, IR3, 1'b1, 1'b0, IR15, IRC0, IRC1, IRC2, IRC3
  // IC_7408 ic_7408_2: pin names not known; wires that end beside it: IRC0, IRC1, IRC2, IR4, IR5, IR6, IR7, IRC3, IRC4, IRC5, IRC6, IRC4, IRC5, IRC6, IRC7
  // IC_74374 ic_74374_3: pin names not known; wires that end beside it: BUS0, BUS1, BUS2, BUS3, BUS4, BUS5, BUS6, BUS7, RP0, RP1, RP2, RP3, RP4, RP5, RP6, RP7, IRC13, IRC14
  // IC_74374 ic_74374_4: pin names not known; wires that end beside it: READ_RP, BUS0, BUS1, BUS2, BUS3, BUS4, BUS5, BUS6, 1'b0, A0, A1, A2, A3, A4, A5, A6, A7
  // DIP_74283 dip_74283_1: pin names not known; wires that end beside it: BUS7, READ_A, ADD1, A1, B1, ADD0, A0, B0, 1'b0, 1'b0, B2, A2, ADD2, B3, A3, ADD3, dip_74283_1_p17
  // IC_7404 ic_7404_1: pin names not known; wires that end beside it: A0, A1, A2, A3, A4, A5, A_INV0, A_INV1, A_INV2, A_INV3, A_INV4, A_INV5
  // IC_7404 ic_7404_2: pin names not known; wires that end beside it: A6, A7, A_INV6, A_INV7
  Pull_Resistor pull_resistor_1 (.node(IR_IN0));
  Pull_Resistor pull_resistor_2 (.node(IR_IN1));
  Pull_Resistor pull_resistor_3 (.node(IR_IN2));
  Pull_Resistor pull_resistor_4 (.node(IR_IN3));
  Pull_Resistor pull_resistor_5 (.node(IR_IN4));
  Pull_Resistor pull_resistor_6 (.node(IR_IN5));
  Pull_Resistor pull_resistor_7 (.node(IR_IN6));
  Pull_Resistor pull_resistor_8 (.node(IR_IN7));
  Pull_Resistor pull_resistor_9 (.node(IR_IN8));
  Pull_Resistor pull_resistor_10 (.node(IR_IN9));
  Pull_Resistor pull_resistor_11 (.node(IR_IN10));
  Pull_Resistor pull_resistor_12 (.node(IR_IN11));
  Pull_Resistor pull_resistor_13 (.node(IR_IN12));
  Pull_Resistor pull_resistor_14 (.node(IR_IN13));
  Pull_Resistor pull_resistor_15 (.node(IR_IN14));
  Pull_Resistor pull_resistor_16 (.node(IR_IN15));
  // IC_7486 ic_7486_3: pin names not known; wires that end beside it: IR8, IR9, IR10, IR11, IRC7, IRI8, IRI9, IRI10, IRI11
  // IC_7486 ic_7486_4: pin names not known; wires that end beside it: IRC8, IRC9, IRC10, IR12, IR13, IR14, IR15, IRC11, IRC12, IRI12, IRI13, IRI14, IRI15
  Pull_Resistor pull_resistor_17 (.node(BUS1));
  Pull_Resistor pull_resistor_18 (.node(BUS3));
  Pull_Resistor pull_resistor_19 (.node(BUS5));
  Pull_Resistor pull_resistor_20 (.node(BUS7));
  // NOT_Gate not_2 has open pins: in=CW5, out=open
  Pull_Resistor pull_resistor_21 (.node(BUS0));
  Pull_Resistor pull_resistor_22 (.node(BUS2));
  Pull_Resistor pull_resistor_23 (.node(BUS4));
  Pull_Resistor pull_resistor_24 (.node(BUS6));
  // DIP_74373 dip_74373_2: pin names not known; wires that end beside it: BUS0, RP0, RP1, BUS1, BUS2, RP2, RP3, BUS3, BUS7, RP7, RP6, BUS6, BUS5, RP5, RP4, BUS4, IRC13, IRC14
  // IC_74374 ic_74374_5: pin names not known; wires that end beside it: BUS0, BUS1, BUS2, BUS3, BUS4, BUS5, BUS6, 1'b1, B0, B1, B2, B3, B4, B5, B6, B7
  // DIP_74283 dip_74283_2: pin names not known; wires that end beside it: BUS7, READ_B, ADD5, A5, B5, ADD4, A4, B4, dip_74283_1_p17, B6, A6, ADD6, B7, A7, ADD7, ADDC7, 1'b0
  // IC_7408 ic_7408_3: pin names not known; wires that end beside it: IR8, IR9, IR10, IR11, IRC7, IRC8, IRC9, IRC10, IRC11
  // IC_7408 ic_7408_4: pin names not known; wires that end beside it: IRC8, IRC9, IRC10, IR12, IR13, IR14, IR15, IRC11, IRC12, IRC12, IRC13, IRC14, IRC15
  // IC_7486 ic_7486_5: pin names not known; wires that end beside it: A_INV0, A_INV1, A_INV2, A_INV3, 1'b1, A_NEG0, A_NEG1, A_NEG2, A_NEG3
  // IC_7486 ic_7486_6: pin names not known; wires that end beside it: AC0, AC1, AC2, A_INV4, A_INV5, A_INV6, A_INV7, AC3, AC4, AC5, AC6, A_NEG4, A_NEG5, A_NEG6, A_NEG7
  // IC_74374 ic_74374_6: pin names not known; wires that end beside it: BUS0, BUS1, BUS2, BUS3, BUS4, BUS5, BUS6, IR_O8, IR_O9, IR_O10, IR_O11, IR_O12, IR_O13, IR_O14, IR_O15
  // NOT_Gate not_3 has open pins: in=CW6, out=open
  // DIP_74373 dip_74373_3: pin names not known; wires that end beside it: BUS7, READ_IR_O, BUS0, ADD0, ADD1, BUS1, BUS2, ADD2, ADD3, BUS3, 1'b0, BUS7, ADD7, ADD6, BUS6, BUS5, ADD5, ADD4, BUS4, 1'b1
  // DIP_74373 dip_74373_4: pin names not known; wires that end beside it: IR_IN0, IRI0, IRI1, IR_IN1, IR_IN2, IRI2, IR_IN7, IRI7, IRI6, IR_IN6, IR_IN5, IRI5
  // NOT_Gate not_4 has open pins: in=IR_OE_INV, out=open
  // DIP_74373 dip_74373_5: pin names not known; wires that end beside it: IRI3, IR_IN3, IR_IN0, BUS0, BUS1, IR_IN1, IR_IN2, BUS2, BUS3, IR_IN3, IRI4, IR_IN4, 1'b1, IR_IN7, BUS7, BUS6, IR_IN6, IR_IN5, BUS5, BUS4, IR_IN4, 1'b1
  // NOT_Gate not_5 has open pins: in=IR_OE, out=open
  nor nor_1 (RAM_EN, R1, R2, R3, R4, R7);
  nor nor_2 (IR_OE_INV, IR_OE, RST, 1'b0, 1'b0, 1'b0);
  // IC_7408 ic_7408_5: pin names not known; wires that end beside it: A_INV0, A_INV1, A_INV2, A_INV3, 1'b1, AC0, AC1, AC2, AC3
  // IC_7408 ic_7408_6: pin names not known; wires that end beside it: AC0, AC1, AC2, A_INV4, A_INV5, A_INV6, A_INV7, AC3, AC4, AC5, AC6, AC4, AC5, AC6, AC7
  nor nor_3 (nor_3_out, RP3, RP4, RP5, RP6, RP7);
  nor nor_4 (LIT_EN, CW4, CW5, CW6, CW7, 1'b0);
  // NOT_Gate not_6 has open pins: in=IR_OE_INV, out=open
  // DIP_74373 dip_74373_6: pin names not known; wires that end beside it: IR_IN8, IRI8, IRI9, IR_IN9, IR_IN10, IR_IN15, IRI15, IRI14, IR_IN14, IR_IN13
  // DIP_74373 dip_74373_7: pin names not known; wires that end beside it: IRI10, IRI11, IR_IN11, IR_IN8, IR_O8, IR_O9, IR_IN9, IR_IN10, IR_O10, IR_O11, IR_IN11, IRI13, IRI12, IR_IN12, 1'b1, IR_IN15, IR_O15, IR_O14, IR_IN14, IR_IN13, IR_O13, IR_O12, IR_IN12, 1'b1
  // NOT_Gate not_7 has open pins: in=IR_OE, out=open
  not not_8 (not_8_out, RAM_EN_INV);
  not not_9 (not_9_out, RAM_WE_INV);
  not not_10 (not_10_out, CW4_INV);
  RAM ram_1 (
    .addr({RP7, RP6, RP5, RP4, RP3, RP2, RP1, RP0}), .data({BUS7, BUS6, BUS5, BUS4, BUS3, BUS2, BUS1, BUS0}),
    .sel(not_8_out), .clk(not_9_out), .ld(not_10_out));  // open: clr
  // IC_7408 ic_7408_7: pin names not known; wires that end beside it: CLK, RP0, RP1, RP2, CW1, nor_3_out, nor_3_out, READ_RP, C_RP0, C_RP1, C_RP2
  // IC_7411 ic_7411_1: pin names not known; wires that end beside it: C_RP0, C_RP0_INV, C_RP0, C_RP1_INV, C_RP1, C_RP1, C_RP2_INV, nor_3_out, R1, R2, R3
  // NOT_Gate not_11 has open pins: in=CW7, out=open
  // DIP_74373 dip_74373_8: pin names not known; wires that end beside it: C_RP2_INV, C_RP2_INV, BUS0, A_NEG0, A_NEG1, BUS1, BUS2, A_NEG2, A_NEG3, BUS3, BUS7, A_NEG7, A_NEG6, BUS6, BUS5, A_NEG5, A_NEG4, BUS4, 1'b1
  // IC_7411 ic_7411_2: pin names not known; wires that end beside it: C_RP0_INV, C_RP0, CLK, C_RP1_INV, C_RP1, CW0, C_RP2, C_RP2, R7, R4, R7, CLK_HW, R2
  // IC_7408 ic_7408_8: pin names not known; wires that end beside it: R3, R4, CLK, CLK, A7, ic_7408_8_p6, ic_7408_8_p7, READ_A, READ_B
  // IC_7408 ic_7408_9: pin names not known; wires that end beside it: A7, CW2, CW3, ic_7408_9_p4, ic_7408_9_p5, CW0, R1_INV, R2_INV, CLK, ic_7408_9_p10, ic_7408_9_p11, RAM_WE
  nor nor_5 (READ_IR_O, ic_7408_9_p10, RAM_WE_INV);
  nor nor_6 (IR_OE, ic_7408_9_p11, RAM_WE_INV);
  // IC_7404 ic_7404_3: pin names not known; wires that end beside it: C_RP0, C_RP1, C_RP2, R2, ic_7408_8_p7, ic_7408_8_p6, C_RP0_INV, C_RP1_INV, C_RP2_INV, R2_INV, ic_7408_9_p5, ic_7408_9_p4
  // IC_7404 ic_7404_4: pin names not known; wires that end beside it: CLK, CW4, RAM_EN, RAM_WE, R1, CLK2, CW4_INV, RAM_EN_INV, RAM_WE_INV, R1_INV, R2_INV

  // Other names for the same wires on the sheet: IR_O0 = BUS0; IR_O1 = BUS1; IR_O2 = BUS2; IR_O3 = BUS3; IR_O4 = BUS4;
  //   IR_O5 = BUS5; IR_O6 = BUS6; IR_O7 = BUS7

  // Notes on the sheet:
  //   contents of rom_1 (hex, n*v repeats v):
  //   2 1 2 1 0 2 14 8 2 41 2 1 2 18 2 14 84 44 8 2 1 2 1 84 2 1 2 1 2 1 2 1 2 1 0 2 1 0 2 14 8 44 2 1 2 1
  //   2 1 2 1 2 1 0 2 14 8 2 41 2 14 8 2 41 2 1 2 18 2 14 84 44 8 2 1 2 1 2 1 2 1 2 1 0 2 1 0 2 14 8 44 2
  //   1 2 1 2 1 2 1 2 14 8 2 41 2 18 2 14 84 2 41 0 2 1 2 14 8 2 41 0 2 14 8 2 41 2 1 2 18 2 14 84 44 8 84
  //   2 1 2 1 2 1 2 1 2 1 0 2 1 0 2 14 8 44 2 1 2 1 2 14 8 2 41 2 1 2 18 2 14 2 41 2 14 8 2 41 2 1 2 14 8
  //   2 41 2 1 0 2 14 2 1 2 1 2 14 8 41 2 14 84 2 18 41 2 1 2 1 0 2 1 2 1 0 2 14 8 2 41 2 1 2 18 2 14 84 2
  //   41 0 2 14 8 2 41 2 1 2 18 2 14 84 44 8 84 8 44 2 1 2 1 2 1 2 1 2 1 0 2 1 0 2 14 8 44 2 1 2 1 2 14 8
  //   2 41 2 1 0 2 14 8 2 41 2 14 8 2 41 2 18 2 14 84 44 8 2 1 2 1 2 1 2 1 2 1 0 2 1 0 2 14 8 44 2 1 2 1 2
  //   14 8 2 41 2 1 2 14 8 2 41 2 1 0 2 14 2 1 2 1 2 14 8 41 2 14 84 2 18 41 2 1 2 1 0 2 14 8 2 41 2 1 2
  //   18 2 14 2 41 2 1 2 1 0 2 1 2 14 8 2 41 2 1 0 2 14 2 1 2 1 2 14 84 2 18 41 2 1 2 1 0 2 14 2 18 41 2
  //   18 2 14 2 41 2 14 8 2 41 2 1 2 18 2 14 84 2 41 2 1 2 1 0 0 2 14 8 2 41 2 14 2 41 0 2 1 2 1 0 2 14 8
  //   2 41 2 1 2 18 2 14 84 44 8 8 44 2 1 2 1 2 1 2 1 2 1 0 2 1 0 2 14 8 44 2 1 2 1 2 1 0 2 14 8 2 41 2 14
  //   8 2 41 2 18 2 14 84 44 8 2 1 2 1 2 1 2 1 2 1 0 2 1 0 2 14 8 44 2 1 2 1 2 14 8 2 41 2 14 8 2 41 0 2
  //   14 2 1 2 1 2 14 84 2 18 41 2 1 2 1 0 2 14 2 18 41 2 1 2 18 2 14 84 44 8 2 1 2 1 84 2 1 2 1 2 1 2 1 2
  //   1 0 2 1 0 2 14 8 44 2 1 2 1 2 1 2 1 0 2 14 8 2 41 2 1 2 18 2 14 2 41 2 1 2 1 0 2 14 8 2 41 2 1 2 1 2
  //   1 2 1 0 2 1 1 1 2 14 8 2 41 2 1 2 18 2 14 2 41 0 2 14 8 2 41 2 1 2 18 2 14 2 41 2 1 2 1 0 2 7*1 2 14
  //   8 2 41 2 1 2 1 2 1 2 1 0 0 2 1 2 1
  //   contents of rom_2 (hex, n*v repeats v):
  //   1 1 2 b0 0 e 0 0 8 0 9 0 8 0 9 4*0 3 0 4 22 0 3 0 4 22 8 1 1 0 2 25 0 8 0 0 8 0 ff 0 3 0 4 34 7 30 1
  //   1 2 a6 0 e 0 0 f 0 f 0 0 8 0 9 0 8 0 9 4*0 3 0 4 52 8 0 1 0 2 55 0 8 1 0 8 0 ff 0 3 0 4 6e 7 2d 8 0
  //   e 0 0 9 0 8 0 9 0 0 f 0 0 11 0 f 0 0 10 0 0 10 0 0 8 0 9 0 8 0 9 5*0 3 0 4 90 8 0 1 0 2 93 0 8 1 0 8
  //   0 ff 0 3 0 4 d1 11 0 0 8 0 9 1 8 0 9 0 11 0 10 0 0 8 0 9 a 8 0 0 d 0 10 ff 0 d 0 3 0 4 cc 10 0 1 0 9
  //   0 0 d 0 0 1 0 2 b7 0 1 0 2 76 0 11 0 0 8 0 9 1 8 0 9 0 0 12 0 0 12 0 0 8 0 9 0 8 0 9 5*0 ff 0 3 0 4
  //   fc 8 0 1 0 2 ff 0 8 1 0 8 0 ff 0 3 1 4 a5 f 0 0 14 0 13 0 0 13 0 0 8 0 12 0 0 9 0 8 0 9 4*0 3 1 4 2b
  //   8 0 1 1 2 2e 0 8 1 0 8 0 ff 0 3 1 4 6c 14 0 0 8 0 9 a 8 0 0 d 0 14 ff 0 d 0 3 1 4 5a 14 0 1 0 9 0 0
  //   d 0 0 1 1 2 45 0 13 0 0 8 0 9 1 8 0 9 0 13 0 1 1 2 f 0 8 30 14 0 0 9 0 a a 0 9 0 3 1 4 87 a 0 0 9 0
  //   0 1 1 2 76 0 a 0 9 0 0 8 0 9 0 7 0 12 0 0 8 0 9 1 8 0 9 0 0 12 0 1 0 2 e0 0 0 5 0 0 1 0 6 0 2 0 0 15
  //   0 16 2 0 16 0 0 8 0 9 7f 8 0 9 4*0 ff 0 3 1 4 d0 8 0 1 1 2 d3 0 8 1 0 8 0 ff 0 3 2 4 93 17 2 0 17 0
  //   0 8 0 16 0 0 9 0 8 0 9 4*0 3 1 4 fa 8 0 1 1 2 fd 0 8 1 0 8 0 ff 0 3 2 4 61 16 0 0 8 0 17 0 0 9 0 0 8
  //   0 3 2 4 21 9 0 0 8 0 0 1 2 2 10 0 9 0 8 0 0 9 0 8 0 9 4*0 3 2 4 3f 0 3 2 4 3f 8 1 1 2 2 42 0 8 0 0 8
  //   0 ff 0 3 2 4 4f 1 2 2 81 0 17 0 0 8 0 9 1 8 0 9 0 17 0 1 1 2 de 0 16 0 0 e 0 5 2 6 6f 1 0 2 4 0 7 20
  //   2f 20 15 0 0 8 0 9 1 8 0 9 0 15 0 0 16 0 0 8 0 9 1 8 0 9 0 16 0 1 1 2 b5 0 7 74 6f 74 61 6c 3a 20 15
  //   0 0 e 0 5 2 6 a9 1 0 2 4 0 0 1 2 2 aa
endmodule
